# Fritzing sketch PirSenzorAlarm (saved by Fritzing 0.9.3b)
breadboards: 1

parts:
  Part1 = Arduino Nano (Rev3.0)
  R1 = Resistor [tolerance=±5% resistance=220 package=THT]
  J1 = Piezo Speaker
  PIR1 = PIR sensor

nets:
  GND: Part1.GND, J1.pin1, PIR1.GND
  N1: Part1.D2, R1.Pin_0
  5V: Part1.5V, PIR1.VDD
  N2: R1.Pin_1, PIR1.SIG
